// Logisim project Cache.circ as structural Verilog: 8 circuits, main circuit main
module main (
  input  EnableTestHalting,
  input  Set,
  output [9:0] CorrectCounter,
  output [9:0] HitCounter,
  output [9:0] MissCounter,
  output [9:0] TestNumber,
  output [7:0] ByteRead,
  output [7:0] CorrectByteRead,
  output Halt
);

  wire and_3_out, and_4_out, and_5_out, CLK, CmdIsRead, Correct, CpuRead, CpuWrite, DidContain, HaltTesting,
       MaxItersReached, MemRead, MemWrite, not_1_out, not_2_out, not_4_out, NotDoneTesting, Ok2Count,
       or_1_out, Ready;
  wire [7:0] CpuWriteValue, MemAddress;
  wire [9:0] CpuAddress;
  wire [31:0] Line2Mem, LineFromMem;

  not not_1 (not_1_out, Ready);
  Clock clock_1 (.out(CLK));
  or or_1 (or_1_out, MaxItersReached, Ready);
  Counter #(.width(4), .max('h9)) MaxClocks (
    .load(Ready), .D(4'b0001), .count(not_1_out), .carry(MaxItersReached), .clk(CLK));  // open: Q, clr
  and and_1 (HaltTesting, EnableTestHalting, CmdIsRead, not_2_out);
  not not_2 (not_2_out, Correct);
  not not_3 (NotDoneTesting, Halt);
  Inputs inputs_1 (
    .HaltTesting(HaltTesting), .Ready(or_1_out), .CLK(CLK), .Done(Halt), .Read(CpuRead), .Write(CpuWrite),
    .Address(CpuAddress), .Value(CpuWriteValue), .TestNumber(TestNumber));
  Cache cache_1 (
    .CpuAddress(CpuAddress), .CpuRead(CpuRead), .CpuWrite(CpuWrite), .CpuWriteValue(CpuWriteValue),
    .CLK(CLK), .Ready(Ready), .DidContain(DidContain), .ByteRead(ByteRead), .MemAddress(MemAddress),
    .MemRead(MemRead), .MemWrite(MemWrite), .LineFromMem(LineFromMem), .Line2Mem(Line2Mem));
  // Probe on CpuRead
  // Probe on CpuWrite
  // Probe on CpuAddress
  // Probe on CpuWriteValue
  // Probe on TestNumber
  // Probe on CorrectByteRead
  // Probe on Correct
  // Probe on Ready
  // Probe on DidContain
  // Probe on ByteRead
  // Probe on MemAddress
  // Probe on MemRead
  // Probe on MemWrite
  // Probe on HitCounter
  // Probe on LineFromMem
  // Probe on Line2Mem
  not not_4 (not_4_out, HaltTesting);
  RAM #(.dataWidth(32), .bus("separate")) ram_1 (
    .addr(MemAddress), .din(Line2Mem), .data(LineFromMem), .str(MemWrite), .clk(CLK), .ld(MemRead));  // open: sel, clr
  and and_2 (Ok2Count, Ready, not_4_out, NotDoneTesting);
  and and_3 (and_3_out, Correct, Ok2Count);
  and and_4 (and_4_out, DidContain, Ok2Count);
  and and_5 (and_5_out, MemRead, NotDoneTesting);
  Checker checker_1 (
    .TestNumber(TestNumber), .YourByteRead(ByteRead), .CmdIsRead(CmdIsRead),
    .CorrectByteRead(CorrectByteRead), .Correct(Correct));
  Counter #(.width(10), .max('h3ff)) u_CorrectCounter (
    .count(and_3_out), .Q(CorrectCounter), .clk(CLK));  // open: load, D, carry, clr
  Counter #(.width(10), .max('h3ff)) u_HitCounter (
    .count(and_4_out), .Q(HitCounter), .clk(CLK));  // open: load, D, carry, clr
  Counter #(.width(10), .max('h3ff)) u_MissCounter (
    .count(and_5_out), .Q(MissCounter), .clk(CLK));  // open: load, D, carry, clr
  // Probe on CorrectCounter
  // Probe on HitCounter
  // Probe on MissCounter

  // Other names for the same wires on the sheet: DoneTesting = Halt

  // Notes on the sheet:
  //   Your Answer Inside Here
endmodule

module Cache (
  input  [9:0] CpuAddress,
  input  CpuRead,
  input  CpuWrite,
  input  [7:0] CpuWriteValue,
  input  CLK,
  input  [31:0] LineFromMem,
  output Ready,
  output DidContain,
  output [7:0] ByteRead,
  output [7:0] MemAddress,
  output MemRead,
  output MemWrite,
  output [31:0] Line2Mem
);

  wire contain_a, contain_b, dirty, dirty_a, dirty_b, isdirty, multiplexer_1_out, n_age, n_dirty, n_tag,
       n_valid, nand_1_out, nand_2_out, nand_3_out, nand_4_out, nand_5_out, nand_6_out, nand_7_out,
       nand_8_out, nand_9_out, nand_10_out, nand_11_out, nand_12_out, nand_13_out, nand_14_out, nand_15_out,
       nand_16_out, nand_17_out, nand_18_out, nand_19_out, nand_20_out, nand_21_out, nand_22_out,
       nand_23_out, nand_24_out, nand_25_out, nand_26_out, nand_27_out, nand_28_out, nand_29_out,
       nand_30_out, nand_31_out, nand_32_out, nand_33_out, nand_34_out, nand_35_out, nand_36_out,
       nand_37_out, nand_38_out, nand_39_out, nand_40_out, nand_41_out, nand_42_out, nand_43_out,
       nand_44_out, nand_45_out, normAge, read_out, saveInputs, saveLine, set_a, set_b, start_a, start_b,
       startContained, valid, valid_a, valid_b, write, write_out, wVal;
  wire [2:0] fsm_1_n0, state_a;
  wire [6:0] p_tag_a, p_tag_b;
  wire [7:0] multiplexer_2_out, readbyte_a, readbyte_b, write2cpu;
  wire [9:0] addr;
  wire [31:0] readline_a, readline_b;

  Demultiplexer #(.enable("false")) demultiplexer_1 (.out0(set_a), .out1(set_b), .in(1'b1), .sel(addr[2]));
  Register #(.width(10)) address (.D(CpuAddress), .en(saveInputs), .Q(addr), .clk(CLK));  // open: clr
  Register #(.width(1)) read (.D(CpuRead), .en(saveInputs), .Q(read_out), .clk(CLK));  // open: clr
  Register #(.width(1)) u_write (.D(CpuWrite), .en(saveInputs), .Q(write_out), .clk(CLK));  // open: clr
  Register writeVal (.D(CpuWriteValue), .en(saveInputs), .Q(write2cpu), .clk(CLK));  // open: clr
  or or_1 (start_a, normAge, set_a);
  or or_2 (start_b, normAge, set_b);
  FSM fsm_1 (
    .p2(state_a[2]), .p1(state_a[1]), .p0(state_a[0]), .CpuRead(read_out), .CpuWrite(write_out),
    .isFound(DidContain), .dirty(isdirty), .n2(fsm_1_n0[2]), .n1(fsm_1_n0[1]), .n0(fsm_1_n0[0]),
    .ready(Ready), .normAge(normAge), .startContained(startContained), .saveInputs(saveInputs),
    .memRead(MemRead), .memWrite(MemWrite), .valid(valid), .newDirty(dirty));
  nand nand_1 (nand_1_out, state_a[2], state_a[2]);
  nand nand_2 (nand_2_out, DidContain, DidContain);
  nand nand_3 (nand_3_out, isdirty, isdirty);
  nand nand_4 (nand_4_out, state_a[1], state_a[1]);
  nand nand_5 (nand_5_out, state_a[0], state_a[0]);
  nand nand_6 (nand_6_out, state_a[2], state_a[2]);
  nand nand_7 (nand_7_out, DidContain, DidContain);
  nand nand_8 (nand_8_out, isdirty, isdirty);
  nand nand_9 (nand_9_out, state_a[1], state_a[1]);
  nand nand_10 (nand_10_out, state_a[0], state_a[0]);
  nand nand_11 (nand_11_out, state_a[2], state_a[2]);
  nand nand_12 (nand_12_out, DidContain, DidContain);
  nand nand_13 (nand_13_out, isdirty, isdirty);
  nand nand_14 (nand_14_out, state_a[1], state_a[1]);
  nand nand_15 (nand_15_out, state_a[0], state_a[0]);
  nand nand_16 (nand_16_out, state_a[0], state_a[0]);
  nand nand_17 (nand_17_out, read_out, read_out);
  nand nand_18 (nand_18_out, state_a[2], state_a[2]);
  nand nand_19 (nand_19_out, state_a[1], state_a[1]);
  nand nand_20 (nand_20_out, state_a[0], state_a[0]);
  nand nand_21 (nand_21_out, state_a[2], state_a[2]);
  nand nand_22 (nand_22_out, state_a[1], state_a[1]);
  nand nand_23 (nand_23_out, state_a[2], state_a[2]);
  nand nand_24 (nand_24_out, DidContain, DidContain);
  nand nand_25 (nand_25_out, isdirty, isdirty);
  nand nand_26 (nand_26_out, state_a[1], state_a[1]);
  nand nand_27 (nand_27_out, state_a[0], state_a[0]);
  nand nand_28 (nand_28_out, state_a[2], state_a[2]);
  nand nand_29 (nand_29_out, state_a[0], state_a[0]);
  nand nand_30 (nand_30_out, state_a[0], state_a[0]);
  nand nand_31 (nand_31_out, read_out, read_out);
  Register #(.width(3)) State (.D(fsm_1_n0), .en(1'b1), .Q(state_a), .clk(CLK));  // open: clr
  nand nand_32 (nand_32_out, nand_1_out, state_a[1], state_a[0], nand_2_out, nand_3_out);
  nand nand_33 (nand_33_out, state_a[2], nand_4_out, nand_5_out);
  nand nand_34 (nand_34_out, nand_6_out, state_a[1], state_a[0], nand_7_out, nand_8_out);
  nand nand_35 (nand_35_out, state_a[2], nand_9_out, nand_10_out);
  nand nand_36 (nand_36_out, nand_11_out, state_a[1], state_a[0], nand_12_out, nand_13_out);
  nand nand_37 (nand_37_out, state_a[2], nand_14_out, nand_15_out);
  nand nand_38 (nand_38_out, state_a[2], nand_16_out, nand_17_out);
  nand nand_39 (nand_39_out, nand_18_out, nand_19_out, nand_20_out);
  nand nand_40 (nand_40_out, nand_21_out, state_a[1], state_a[0], DidContain);
  nand nand_41 (nand_41_out, state_a[2], nand_22_out, state_a[0]);
  nand nand_42 (nand_42_out, nand_23_out, state_a[1], state_a[0], nand_24_out, nand_25_out);
  nand nand_43 (nand_43_out, state_a[2], nand_26_out, nand_27_out);
  nand nand_44 (nand_44_out, nand_28_out, state_a[1], nand_29_out);
  nand nand_45 (nand_45_out, state_a[2], state_a[1], nand_30_out, nand_31_out);
  nand nand_46 (n_tag, nand_32_out, nand_33_out);
  nand nand_47 (n_valid, nand_34_out, nand_35_out);
  nand nand_48 (n_dirty, nand_36_out, nand_37_out, nand_38_out);
  nand nand_49 (n_age, nand_39_out, nand_40_out, nand_41_out);
  nand nand_50 (write, nand_42_out, nand_43_out);
  nand nand_51 (saveLine, nand_44_out, nand_44_out);
  nand nand_52 (wVal, nand_45_out, nand_45_out);
  Multiplexer #(.enable("false")) multiplexer_1 (
    .in0(contain_a), .in1(contain_b), .out(multiplexer_1_out), .sel(addr[2]));
  Multiplexer #(.width(8), .enable("false")) multiplexer_2 (
    .in0({p_tag_a, 1'b0}), .in1({p_tag_b, 1'b1}), .out(multiplexer_2_out), .sel(addr[2]));
  Sets sets_1 (
    .start(start_a), .CLK(CLK), .tag(addr[9:3]), .valid(valid), .dirty(dirty), .new_tag(n_tag),
    .new_age(n_age), .new_valid(n_valid), .new_dirty(n_dirty), .saveLine(saveLine), .normAge(normAge),
    .LineFromMem(LineFromMem), .offset(addr[1:0]), .write(write), .wval(wVal), .CpuWriteValue(write2cpu),
    .currTag(p_tag_a), .isValid(valid_a), .isDirty(dirty_a), .LineRead(readline_a), .ByteRead(readbyte_a),
    .DidContain(contain_a));
  Multiplexer #(.enable("false")) multiplexer_3 (.in0(dirty_a), .in1(dirty_b), .out(isdirty), .sel(addr[2]));
  Multiplexer #(.width(32), .enable("false")) multiplexer_4 (
    .in0(readline_a), .in1(readline_b), .out(Line2Mem), .sel(addr[2]));
  Multiplexer #(.width(8), .enable("false")) multiplexer_5 (
    .in0(readbyte_a), .in1(readbyte_b), .out(ByteRead), .sel(addr[2]));
  Register #(.width(1)) u_DidContain (
    .D(multiplexer_1_out), .en(startContained), .Q(DidContain), .clk(CLK));  // open: clr
  Multiplexer #(.width(8), .enable("false")) multiplexer_6 (
    .in0(addr[9:2]), .in1(multiplexer_2_out), .out(MemAddress), .sel(MemWrite));
  Sets sets_2 (
    .start(start_b), .CLK(CLK), .tag(addr[9:3]), .valid(valid), .dirty(dirty), .new_tag(n_tag),
    .new_age(n_age), .new_valid(n_valid), .new_dirty(n_dirty), .saveLine(saveLine), .normAge(normAge),
    .LineFromMem(LineFromMem), .offset(addr[1:0]), .write(write), .wval(wVal), .CpuWriteValue(write2cpu),
    .currTag(p_tag_b), .isValid(valid_b), .isDirty(dirty_b), .LineRead(readline_b), .ByteRead(readbyte_b),
    .DidContain(contain_b));

  // Other names for the same wires on the sheet: offset[1:0] = addr[1:0]; set = addr[2]; tag[6:0] = addr[9:3];
  //   isFound = DidContain; MemAddr[7:0] = MemAddress

  // Notes on the sheet:
  //   Address Bits = 10
  //   Line Size = 4
  //   W = 3
  //   Num Sets = 2
  //   C =4*3*2 = 24bytes
  //   Tag bits = 7
endmodule

module Inputs (
  input  HaltTesting,
  input  Ready,
  input  CLK,
  output Done,
  output Read,
  output Write,
  output [9:0] Address,
  output [7:0] Value,
  output [9:0] TestNumber
);

  wire and_1_out, not_1_out, not_2_out;

  not not_1 (not_1_out, HaltTesting);
  not not_2 (not_2_out, Done);
  Counter #(.width(10), .max('h3ff), .ongoal("stay")) u_TestNumber (
    .count(and_1_out), .Q(TestNumber), .clk(CLK));  // open: load, D, carry, clr
  and and_1 (and_1_out, not_1_out, Ready, not_2_out);
  ROM #(.addrWidth(10), .dataWidth(21)) rom_1 (
    .addr(TestNumber), .data({Done, Read, Write, Address, Value}));  // open: sel

  // Notes on the sheet:
  //   contents of rom_1 (hex, n*v repeats v):
  //   80882 83fe6 4306b 83e0e 43701 42275 8280f 80304 41bd8 84371 43f77 41d70 4250b 44733 8253d 440d8
  //   82691 440c9 83d7c 43558 446bf 83837 842c9 43e0f 4059d 41556 80166 833b0 43a89 83142 8361c 42e66
  //   43eb6 42c00 43a0e 8165c 84682 8092a 83907 41f89 817b0 40855 82056 425e8 43ff2 8039f 42bd7 82137
  //   4416b 40273 8324a 814e4 44570 41c0f 429da 82640 8069c 8099e 414d5 41004 81beb 84113 419b1 81add
  //   83f35 425ff 829cd 40250 82945 4366d 40cc2 444f8 80814 81156 8446d 42a82 42bae 82578 41135 405d0
  //   8304b 82b3a 40972 822ba 4443a 42337 82506 80bd3 80560 83552 83955 81434 43096 43da1 81aa2 80305
  //   428e6 428cc 808a2 40e80 845f0 4215d 82765 82e29 40be5 82b74 42715 417a2 41fab 8452f 81c0a 83325
  //   44624 80205 42dfc 41333 40958 81348 42736 41069 84510 44669 826dd 8067e 408e4 44680 444e8 832ad
  //   821f8 83509 82d46 81184 432cd 80b77 4005a 440e0 81ea0 43d73 42b8c 80624 41468 42699 415ed 80fc1 0
  //   100000
endmodule

module Checker (
  input  [9:0] TestNumber,
  input  [7:0] YourByteRead,
  output CmdIsRead,
  output [7:0] CorrectByteRead,
  output Correct
);

  wire comparator_1_eq;
  wire [9:0] subtractor_1_out;

  // Probe on TestNumber
  Subtractor #(.width(10)) subtractor_1 (.a(TestNumber), .b(10'h1), .out(subtractor_1_out));  // open: bin, bout
  ROM #(.addrWidth(10), .dataWidth(9)) rom_1 (
    .addr(subtractor_1_out), .data({CmdIsRead, CorrectByteRead}));  // open: sel
  Comparator #(.mode("unsigned")) comparator_1 (
    .a(YourByteRead), .b(CorrectByteRead), .eq(comparator_1_eq));  // open: gt, lt
  and and_1 (Correct, comparator_1_eq, CmdIsRead);

  // Other names for the same wires on the sheet: Test_Number[9:0] = TestNumber

  // Notes on the sheet:
  //   Read Solutions
  //   contents of rom_1 (hex, n*v repeats v):
  //   1a3 1dc 6b 125 1 75 1dc 1c3 d8 1ab 77 70 b 33 10b d8 1c3 c9 174 58 bf 153 199 f 9d 56 1bb 13b 89 16c
  //   180 66 b6 0 e 107 1bf 1d8 167 89 118 55 1a2 e8 f2 1c3 d7 142 6b 73 1ab 18c 70 f da 1c3 14c 1d8 d5 4
  //   1d8 16b b1 1f4 1f2 ff 1da 50 1da 6d c2 f8 155 1c6 1f8 82 ae 1ff 35 d0 16b 1ae 72 175 3a 37 1ff 173
  //   1d0 158 167 1d5 96 a1 1f4 1c3 e6 cc 155 80 170 5d 1e6 166 e5 1ae 15 a2 ab 170 10f 13b 24 150 fc 33
  //   58 133 36 69 170 69 1c3 14c e4 80 e8 1ab 15d 158 1fc 135 cd 1e5 5a e0 104 73 8c 14c 68 99 ed 1a6
endmodule

module Sets (
  input  start,
  input  [6:0] tag,
  input  valid,
  input  dirty,
  input  new_tag,
  input  new_age,
  input  new_valid,
  input  new_dirty,
  input  saveLine,
  input  normAge,
  input  [1:0] offset,
  input  [31:0] LineFromMem,
  input  write,
  input  wval,
  input  [7:0] CpuWriteValue,
  input  CLK,
  output [6:0] currTag,
  output isValid,
  output isDirty,
  output [31:0] LineRead,
  output [7:0] ByteRead,
  output DidContain
);

  wire comparator_1_eq, comparator_2_eq, comparator_3_eq, dirty_a, dirty_b, dirty_c, found_a, found_b,
       found_c, n_dirty_00, n_dirty_01, n_dirty_10, n_tag_00, n_tag_01, n_tag_10, n_valid_00, n_valid_01,
       n_valid_10, NotFound, old_a, old_b, old_c, startStoreLine, valid_a, valid_b, valid_c, write_00,
       write_01, write_10, wVal_00, wVal_01, wVal_10;
  wire [1:0] multiplexer_1_out, multiplexer_2_out, multiplexer_3_out, multiplexer_4_out, multiplexer_5_out,
       nxt_age_a, nxt_age_b, nxt_age_c, offest, oldest, p_age_a, p_age_b, p_age_c, SelectedLine, t_age_a,
       t_age_b, t_age_c;
  wire [6:0] p_tag_a, p_tag_b, p_tag_c;
  wire [7:0] byte_a, byte_b, byte_c;
  wire [31:0] p_line_a, p_line_b, p_line_c;

  Lines lines_1 (
    .start(start), .pTag(p_tag_a), .pAge(p_age_a), .tag(tag), .isValid(valid_a), .age(nxt_age_a),
    .isDirty(dirty_a), .valid(valid), .dirty(dirty), .new_tag(n_tag_00), .new_age(new_age),
    .new_valid(n_valid_00), .new_dirty(n_dirty_00), .offset(offest), .LineFromMem(LineFromMem),
    .currLine(p_line_a), .write(write_00), .wval(wVal_00), .CpuWriteValue(CpuWriteValue), .ByteRead(byte_a),
    .CLK(CLK));
  Lines lines_2 (
    .start(start), .pTag(p_tag_b), .pAge(p_age_b), .tag(tag), .isValid(valid_b), .age(nxt_age_b),
    .isDirty(dirty_b), .valid(valid), .dirty(dirty), .new_tag(n_tag_01), .new_age(new_age),
    .new_valid(n_valid_01), .new_dirty(n_dirty_01), .offset(offest), .LineFromMem(LineFromMem),
    .currLine(p_line_b), .write(write_01), .wval(wVal_01), .CpuWriteValue(CpuWriteValue), .ByteRead(byte_b),
    .CLK(CLK));
  Lines lines_3 (
    .start(start), .pTag(p_tag_c), .pAge(p_age_c), .tag(tag), .isValid(valid_c), .age(nxt_age_c),
    .isDirty(dirty_c), .valid(valid), .dirty(dirty), .new_tag(n_tag_10), .new_age(new_age),
    .new_valid(n_valid_10), .new_dirty(n_dirty_10), .offset(offest), .LineFromMem(LineFromMem),
    .currLine(p_line_c), .write(write_10), .wval(wVal_10), .CpuWriteValue(CpuWriteValue), .ByteRead(byte_c),
    .CLK(CLK));
  Comparator #(.width(7), .mode("unsigned")) comparator_1 (.a(p_tag_a), .b(tag), .eq(comparator_1_eq));  // open: gt, lt
  Comparator #(.width(7), .mode("unsigned")) comparator_2 (.a(p_tag_b), .b(tag), .eq(comparator_2_eq));  // open: gt, lt
  Comparator #(.width(7), .mode("unsigned")) comparator_3 (.a(p_tag_c), .b(tag), .eq(comparator_3_eq));  // open: gt, lt
  and and_1 (startStoreLine, start, saveLine);
  Comparator #(.width(2), .mode("unsigned")) comparator_4 (.a(p_age_a), .b(2'b10), .eq(old_a));  // open: gt, lt
  Comparator #(.width(2), .mode("unsigned")) comparator_5 (.a(p_age_b), .b(2'b10), .eq(old_b));  // open: gt, lt
  Comparator #(.width(2), .mode("unsigned")) comparator_6 (.a(p_age_c), .b(2'b10), .eq(old_c));  // open: gt, lt
  and and_2 (found_a, comparator_1_eq, valid_a);
  and and_3 (found_b, comparator_2_eq, valid_b);
  and and_4 (found_c, comparator_3_eq, valid_c);
  and and_5 (NotFound, ~found_a, ~found_b, ~found_c);  // AND_Gate
  Multiplexer #(.width(2), .enable("false")) multiplexer_1 (
    .in0(2'b10), .in1(2'b10), .out(multiplexer_1_out), .sel(old_c));
  Multiplexer #(.width(2), .enable("false")) multiplexer_2 (
    .in0(oldest), .in1(2'b10), .out(multiplexer_2_out), .sel(found_c));
  Multiplexer #(.width(2), .enable("false")) multiplexer_3 (
    .in0(multiplexer_1_out), .in1(2'b01), .out(multiplexer_3_out), .sel(old_b));
  Multiplexer #(.width(2), .enable("false")) multiplexer_4 (
    .in0(multiplexer_2_out), .in1(2'b01), .out(multiplexer_4_out), .sel(found_b));
  Multiplexer #(.width(2), .enable("false")) multiplexer_5 (
    .in0(multiplexer_4_out), .in1(2'b00), .out(multiplexer_5_out), .sel(found_a));
  Age_Update age_update_1 (
    .Index(SelectedLine), .pAge_a(p_age_a), .pAge_b(p_age_b), .pAge_c(p_age_c), .nAge_a(t_age_a),
    .nAge_b(t_age_b), .nAge_c(t_age_c));
  Multiplexer #(.width(2), .enable("false")) multiplexer_6 (.in0(t_age_a), .in1(2'b00), .out(nxt_age_a), .sel(normAge));
  Multiplexer #(.width(2), .enable("false")) multiplexer_7 (.in0(t_age_b), .in1(2'b01), .out(nxt_age_b), .sel(normAge));
  Multiplexer #(.width(2), .enable("false")) multiplexer_8 (.in0(t_age_c), .in1(2'b10), .out(nxt_age_c), .sel(normAge));
  Multiplexer #(.width(2), .enable("false")) multiplexer_9 (
    .in0(multiplexer_3_out), .in1(2'b00), .out(oldest), .sel(old_a));
  Register #(.width(2)) index (.D(multiplexer_5_out), .en(startStoreLine), .Q(SelectedLine), .clk(CLK));  // open: clr
  Demultiplexer #(.select(2), .enable("false")) demultiplexer_1 (
    .out0(n_tag_00), .out1(n_tag_01), .out2(n_tag_10), .in(new_tag), .sel(SelectedLine));  // open: out3
  Demultiplexer #(.select(2), .enable("false")) demultiplexer_2 (
    .out0(n_valid_00), .out1(n_valid_01), .out2(n_valid_10), .in(new_valid), .sel(SelectedLine));  // open: out3
  Demultiplexer #(.select(2), .enable("false")) demultiplexer_3 (
    .out0(n_dirty_00), .out1(n_dirty_01), .out2(n_dirty_10), .in(new_dirty), .sel(SelectedLine));  // open: out3
  Demultiplexer #(.select(2), .enable("false")) demultiplexer_4 (
    .out0(write_00), .out1(write_01), .out2(write_10), .in(write), .sel(SelectedLine));  // open: out3
  Demultiplexer #(.select(2), .enable("false")) demultiplexer_5 (
    .out0(wVal_00), .out1(wVal_01), .out2(wVal_10), .in(wval), .sel(SelectedLine));  // open: out3
  Multiplexer #(.select(2), .width(8), .enable("false")) multiplexer_10 (
    .in0(byte_a), .in1(byte_b), .in2(byte_c), .out(ByteRead), .sel(SelectedLine));  // open: in3
  not not_1 (DidContain, NotFound);
  Multiplexer #(.select(2), .width(7), .enable("false")) multiplexer_11 (
    .in0(p_tag_a), .in1(p_tag_b), .in2(p_tag_c), .out(currTag), .sel(SelectedLine));  // open: in3
  Multiplexer #(.select(2), .enable("false")) multiplexer_12 (
    .in0(valid_a), .in1(valid_b), .in2(valid_c), .out(isValid), .sel(SelectedLine));  // open: in3
  Multiplexer #(.select(2), .enable("false")) multiplexer_13 (
    .in0(dirty_a), .in1(dirty_b), .in2(dirty_c), .out(isDirty), .sel(SelectedLine));  // open: in3
  Multiplexer #(.select(2), .width(32), .enable("false")) multiplexer_14 (
    .in0(p_line_a), .in1(p_line_b), .in2(p_line_c), .out(LineRead), .sel(SelectedLine));  // open: in3

  // Other names for the same wires on the sheet: n_age = new_age; n_dirty = new_dirty; n_tag = new_tag;
  //   n_valid = new_valid
endmodule

module Lines (
  input  start,
  input  [6:0] tag,
  input  [1:0] age,
  input  valid,
  input  dirty,
  input  new_tag,
  input  new_age,
  input  new_valid,
  input  new_dirty,
  input  [1:0] offset,
  input  [31:0] LineFromMem,
  input  write,
  input  wval,
  input  [7:0] CpuWriteValue,
  input  CLK,
  output [6:0] pTag,
  output [1:0] pAge,
  output isValid,
  output isDirty,
  output [31:0] currLine,
  output [7:0] ByteRead
);

  wire and_6_out, demultiplexer_1_out0, demultiplexer_1_out1, demultiplexer_1_out2, demultiplexer_1_out3,
       or_1_out, or_2_out, or_3_out, or_4_out, startAge, startDirty, startTag, startValid, startWrite;
  wire [7:0] _00, _01, _10, _11;

  Register #(.width(1)) Valid_Bit (.D(valid), .en(startValid), .Q(isValid), .clk(CLK));  // open: clr
  Register #(.width(1)) Dirty_Bit (.D(dirty), .en(startDirty), .Q(isDirty), .clk(CLK));  // open: clr
  Register #(.width(7)) Tag_Bits (.D(tag), .en(startTag), .Q(pTag), .clk(CLK));  // open: clr
  Register #(.width(2)) u_Age (.D(age), .en(startAge), .Q(pAge), .clk(CLK));  // open: clr
  and and_1 (startTag, start, new_tag);
  and and_2 (startAge, start, new_age);
  and and_3 (startValid, start, new_valid);
  and and_4 (startDirty, start, new_dirty);
  and and_5 (startWrite, start, write);
  Demultiplexer #(.select(2), .enable("false")) demultiplexer_1 (
    .out0(demultiplexer_1_out0), .out1(demultiplexer_1_out1), .out2(demultiplexer_1_out2),
    .out3(demultiplexer_1_out3), .in(and_6_out), .sel(offset));
  and and_6 (and_6_out, start, wval);
  Multiplexer #(.width(8), .enable("false")) multiplexer_1 (
    .in0(LineFromMem[7:0]), .in1(CpuWriteValue), .out(_00), .sel(wval));
  Multiplexer #(.width(8), .enable("false")) multiplexer_2 (
    .in0(LineFromMem[15:8]), .in1(CpuWriteValue), .out(_01), .sel(wval));
  Multiplexer #(.width(8), .enable("false")) multiplexer_3 (
    .in0(LineFromMem[23:16]), .in1(CpuWriteValue), .out(_10), .sel(wval));
  Multiplexer #(.width(8), .enable("false")) multiplexer_4 (
    .in0(LineFromMem[31:24]), .in1(CpuWriteValue), .out(_11), .sel(wval));
  or or_1 (or_1_out, startWrite, demultiplexer_1_out0);
  or or_2 (or_2_out, startWrite, demultiplexer_1_out1);
  or or_3 (or_3_out, startWrite, demultiplexer_1_out2);
  or or_4 (or_4_out, startWrite, demultiplexer_1_out3);
  Register Val00 (.D(_00), .en(or_1_out), .Q(currLine[7:0]), .clk(CLK));  // open: clr
  Register Val01 (.D(_01), .en(or_2_out), .Q(currLine[15:8]), .clk(CLK));  // open: clr
  Register Val10 (.D(_10), .en(or_3_out), .Q(currLine[23:16]), .clk(CLK));  // open: clr
  Register Val11 (.D(_11), .en(or_4_out), .Q(currLine[31:24]), .clk(CLK));  // open: clr
  Multiplexer #(.select(2), .width(8), .enable("false")) multiplexer_5 (
    .in0(currLine[7:0]), .in1(currLine[15:8]), .in2(currLine[23:16]), .in3(currLine[31:24]), .out(ByteRead),
    .sel(offset));

  // Other names for the same wires on the sheet: n_age = new_age; n_dirty = new_dirty; n_tag = new_tag;
  //   n_valid = new_valid; p_age[1:0] = pAge; p_tag[6:0] = pTag
endmodule

module Age_Update (
  input  [1:0] Index,
  input  [1:0] pAge_a,
  input  [1:0] pAge_b,
  input  [1:0] pAge_c,
  output [1:0] nAge_a,
  output [1:0] nAge_b,
  output [1:0] nAge_c
);

  wire comparator_1_eq, comparator_1_lt, comparator_2_eq, comparator_2_lt, comparator_3_eq, comparator_3_lt;
  wire [1:0] adder_1_out, adder_2_out, adder_3_out, makeNewAge, multiplexer_2_out, multiplexer_3_out,
       multiplexer_4_out;

  Multiplexer #(.select(2), .width(2), .enable("false")) multiplexer_1 (
    .in0(pAge_a), .in1(pAge_b), .in2(pAge_c), .out(makeNewAge), .sel(Index));  // open: in3
  Comparator #(.width(2), .mode("unsigned")) comparator_1 (
    .a(pAge_a), .b(makeNewAge), .eq(comparator_1_eq), .lt(comparator_1_lt));  // open: gt
  Comparator #(.width(2), .mode("unsigned")) comparator_2 (
    .a(pAge_b), .b(makeNewAge), .eq(comparator_2_eq), .lt(comparator_2_lt));  // open: gt
  Comparator #(.width(2), .mode("unsigned")) comparator_3 (
    .a(pAge_c), .b(makeNewAge), .eq(comparator_3_eq), .lt(comparator_3_lt));  // open: gt
  Multiplexer #(.width(2), .enable("false")) multiplexer_2 (
    .in0(pAge_a), .in1(2'b00), .out(multiplexer_2_out), .sel(comparator_1_eq));
  Multiplexer #(.width(2), .enable("false")) multiplexer_3 (
    .in0(pAge_b), .in1(2'b00), .out(multiplexer_3_out), .sel(comparator_2_eq));
  Multiplexer #(.width(2), .enable("false")) multiplexer_4 (
    .in0(pAge_c), .in1(2'b00), .out(multiplexer_4_out), .sel(comparator_3_eq));
  Multiplexer #(.width(2), .enable("false")) multiplexer_5 (
    .in0(multiplexer_2_out), .in1(adder_1_out), .out(nAge_a), .sel(comparator_1_lt));
  Adder #(.width(2)) adder_1 (.a(pAge_a), .b(2'b01), .out(adder_1_out));  // open: cin, cout
  Multiplexer #(.width(2), .enable("false")) multiplexer_6 (
    .in0(multiplexer_3_out), .in1(adder_2_out), .out(nAge_b), .sel(comparator_2_lt));
  Adder #(.width(2)) adder_2 (.a(pAge_b), .b(2'b01), .out(adder_2_out));  // open: cin, cout
  Multiplexer #(.width(2), .enable("false")) multiplexer_7 (
    .in0(multiplexer_4_out), .in1(adder_3_out), .out(nAge_c), .sel(comparator_3_lt));
  Adder #(.width(2)) adder_3 (.a(pAge_c), .b(2'b01), .out(adder_3_out));  // open: cin, cout

  // Other names for the same wires on the sheet: n_age_a[1:0] = nAge_a; n_age_b[1:0] = nAge_b; n_age_c[1:0] = nAge_c;
  //   p_age_a[1:0] = pAge_a; p_age_b[1:0] = pAge_b; p_age_c[1:0] = pAge_c
endmodule

module FSM (
  input  p2,
  input  p1,
  input  p0,
  input  CpuRead,
  input  CpuWrite,
  input  isFound,
  input  dirty,
  output n2,
  output n1,
  output n0,
  output ready,
  output normAge,
  output startContained,
  output saveInputs,
  output memRead,
  output memWrite,
  output valid,
  output newDirty
);

  wire nand_1_out, nand_2_out, nand_3_out, nand_4_out, nand_5_out, nand_6_out, nand_7_out, nand_8_out,
       nand_9_out, nand_10_out, nand_11_out, nand_12_out, nand_13_out, nand_14_out, nand_15_out, nand_16_out,
       nand_17_out, nand_18_out, nand_19_out, nand_20_out, nand_21_out, nand_22_out, nand_23_out,
       nand_24_out, nand_25_out, nand_26_out, nand_27_out, nand_28_out, nand_29_out, nand_30_out,
       nand_31_out, nand_32_out, nand_33_out, nand_34_out, nand_35_out, nand_36_out, nand_37_out,
       nand_38_out, nand_39_out, nand_40_out, nand_41_out, nand_42_out, nand_43_out, nand_44_out,
       nand_45_out, nand_46_out, nand_47_out, nand_48_out, nand_49_out, nand_50_out, nand_51_out,
       nand_52_out, nand_53_out, nand_54_out, nand_55_out, nand_56_out, nand_57_out, nand_58_out,
       nand_59_out, nand_60_out, nand_61_out, nand_62_out, nand_63_out, nand_64_out, nand_65_out,
       nand_66_out, nand_67_out, nand_68_out, nand_69_out, nand_70_out, nand_71_out;

  nand nand_1 (nand_1_out, p2, p2);
  nand nand_2 (nand_2_out, p1, p1);
  nand nand_3 (nand_3_out, p0, p0);
  nand nand_4 (nand_4_out, CpuRead, CpuRead);
  nand nand_5 (nand_5_out, p1, p1);
  nand nand_6 (nand_6_out, CpuRead, CpuRead);
  nand nand_7 (nand_7_out, p1, p1);
  nand nand_8 (nand_8_out, CpuWrite, CpuWrite);
  nand nand_9 (nand_9_out, p2, p2);
  nand nand_10 (nand_10_out, p0, p0);
  nand nand_11 (nand_11_out, p0, p0);
  nand nand_12 (nand_12_out, CpuRead, CpuRead);
  nand nand_13 (nand_13_out, p2, p2);
  nand nand_14 (nand_14_out, CpuRead, CpuRead);
  nand nand_15 (nand_15_out, CpuWrite, CpuWrite);
  nand nand_16 (nand_16_out, isFound, isFound);
  nand nand_17 (nand_17_out, dirty, dirty);
  nand nand_18 (nand_18_out, p2, p2);
  nand nand_19 (nand_19_out, p1, p1);
  nand nand_20 (nand_20_out, p2, p2);
  nand nand_21 (nand_21_out, p1, p1);
  nand nand_22 (nand_22_out, p0, p0);
  nand nand_23 (nand_23_out, p2, p2);
  nand nand_24 (nand_24_out, p0, p0);
  nand nand_25 (nand_25_out, p2, p2);
  nand nand_26 (nand_26_out, p1, p1);
  nand nand_27 (nand_27_out, p0, p0);
  nand nand_28 (nand_28_out, p2, p2);
  nand nand_29 (nand_29_out, p1, p1);
  nand nand_30 (nand_30_out, CpuRead, CpuRead);
  nand nand_31 (nand_31_out, p2, p2);
  nand nand_32 (nand_32_out, p1, p1);
  nand nand_33 (nand_33_out, CpuWrite, CpuWrite);
  nand nand_34 (nand_34_out, p2, p2);
  nand nand_35 (nand_35_out, isFound, isFound);
  nand nand_36 (nand_36_out, dirty, dirty);
  nand nand_37 (nand_37_out, p1, p1);
  nand nand_38 (nand_38_out, p0, p0);
  nand nand_39 (nand_39_out, p2, p2);
  nand nand_40 (nand_40_out, isFound, isFound);
  nand nand_41 (nand_41_out, p2, p2);
  nand nand_42 (nand_42_out, isFound, isFound);
  nand nand_43 (nand_43_out, dirty, dirty);
  nand nand_44 (nand_44_out, p1, p1);
  nand nand_45 (nand_45_out, p0, p0);
  nand nand_46 (nand_46_out, p0, p0);
  nand nand_47 (nand_47_out, CpuRead, CpuRead);
  nand nand_48 (nand_48_out, nand_1_out, p1, p0);
  nand nand_49 (nand_49_out, p2, nand_2_out);
  nand nand_50 (nand_50_out, p2, nand_3_out, nand_4_out);
  nand nand_51 (nand_51_out, nand_5_out, p0, nand_6_out, CpuWrite);
  nand nand_52 (nand_52_out, nand_7_out, p0, CpuRead, nand_8_out);
  nand nand_53 (nand_53_out, nand_9_out, p1, nand_10_out);
  nand nand_54 (nand_54_out, p1, nand_11_out, nand_12_out);
  nand nand_55 (nand_55_out, nand_13_out, p1, isFound);
  nand nand_56 (nand_56_out, nand_14_out, nand_15_out);
  nand nand_57 (nand_57_out, CpuRead, CpuWrite);
  nand nand_58 (nand_58_out, p1, nand_16_out, nand_17_out);
  nand nand_59 (nand_59_out, p2, p1);
  nand nand_60 (nand_60_out, nand_18_out, nand_19_out, p0);
  nand nand_61 (nand_61_out, nand_20_out, nand_21_out, nand_22_out);
  nand nand_62 (nand_62_out, nand_23_out, p1, nand_24_out);
  nand nand_63 (nand_63_out, nand_25_out, nand_26_out, nand_27_out);
  nand nand_64 (nand_64_out, nand_28_out, nand_29_out, nand_30_out, CpuWrite);
  nand nand_65 (nand_65_out, nand_31_out, nand_32_out, CpuRead, nand_33_out);
  nand nand_66 (nand_66_out, nand_34_out, p1, p0, nand_35_out, nand_36_out);
  nand nand_67 (nand_67_out, p2, nand_37_out, nand_38_out);
  nand nand_68 (nand_68_out, nand_39_out, p1, p0, nand_40_out, dirty);
  nand nand_69 (nand_69_out, nand_41_out, p1, p0, nand_42_out, nand_43_out);
  nand nand_70 (nand_70_out, p2, nand_44_out, nand_45_out);
  nand nand_71 (nand_71_out, p2, p1, nand_46_out, nand_47_out);
  nand nand_72 (n2, nand_48_out, nand_49_out, nand_50_out);
  nand nand_73 (n1, nand_51_out, nand_52_out, nand_53_out, nand_54_out, nand_55_out);
  nand nand_74 (n0, p0, nand_56_out, nand_57_out, nand_58_out, nand_59_out);
  nand nand_75 (ready, nand_60_out, nand_60_out);
  nand nand_76 (normAge, nand_61_out, nand_61_out);
  nand nand_77 (startContained, nand_62_out, nand_62_out);
  nand nand_78 (saveInputs, nand_63_out, nand_64_out, nand_65_out);
  nand nand_79 (memRead, nand_66_out, nand_67_out);
  nand nand_80 (memWrite, nand_68_out, nand_68_out);
  nand nand_81 (valid, nand_69_out, nand_70_out);
  nand nand_82 (newDirty, nand_71_out, nand_71_out);
endmodule
