// Logisim project 4BitParity.circ as structural Verilog: 5 circuits, main circuit main
module main (
  input  Halt_Enable
);

  wire and_2_out, CLK, Correct, Done_Testing, Halt, Input, not_1_out, not_2_out, not_3_out, Solution,
       YourAnswer;
  wire [6:0] counter_1_q, TestNumber;

  not not_1 (not_1_out, Correct);
  Clock clock_1 (.out(CLK));
  and and_1 (Halt, Halt_Enable, not_1_out);
  Inputs inputs_1 (.Halt(Halt), .CLK(CLK), .Input(Input), .TestNumber(TestNumber), .Done_Testing(Done_Testing));
  _4BitEvenParity u_4bitevenparity_1 (.CLK(CLK), .Input(Input), .Is_Even(YourAnswer));
  // Probe on Input
  // Probe on YourAnswer
  // Probe on Solution
  // Probe on Correct
  not not_2 (not_2_out, Halt);
  and and_2 (and_2_out, Correct, not_2_out, not_3_out);
  not not_3 (not_3_out, Done_Testing);
  Checker checker_1 (.Your_Answer(YourAnswer), .TestNumber(TestNumber), .Correct(Correct), .Solution(Solution));
  Counter #(.width(7), .max('h41), .ongoal("stay")) counter_1 (
    .count(and_2_out), .Q(counter_1_q), .clk(CLK));  // open: load, D, carry, clr
  // Probe on counter_1_q

  // Notes on the sheet:
  //   Max 65
endmodule

module _4BitEvenParity (
  input  CLK,
  input  Input,
  output Is_Even
);

  wire d_ff_1_q, d_ff_2_q, d_ff_3_q, sub_circuit_1_ns0, sub_circuit_1_ns1, sub_circuit_1_ns2;

  Sub_Circuit sub_circuit_1 (
    .B(d_ff_1_q), .C(d_ff_2_q), .D(d_ff_3_q), .ns2(sub_circuit_1_ns2), .\input (Input),
    .ns1(sub_circuit_1_ns1), .ns0(sub_circuit_1_ns0), .\output (Is_Even));  // open: A, ns3
  D_Flip_Flop d_ff_1 (.clk(CLK), .D(sub_circuit_1_ns2), .Q(d_ff_1_q));  // open: Qn, preset, en, reset
  D_Flip_Flop d_ff_2 (.clk(CLK), .D(sub_circuit_1_ns1), .Q(d_ff_2_q));  // open: Qn, preset, en, reset
  D_Flip_Flop d_ff_3 (.clk(CLK), .D(sub_circuit_1_ns0), .Q(d_ff_3_q));  // open: Qn, preset, en, reset
endmodule

module Inputs (
  input  Halt,
  input  CLK,
  output Input,
  output [6:0] TestNumber,
  output Done_Testing
);

  wire not_1_out;

  not not_1 (not_1_out, Halt);
  Counter #(.width(7), .max('h41), .ongoal("stay")) counter_1 (
    .count(not_1_out), .Q(TestNumber), .carry(Done_Testing), .clk(CLK));  // open: load, D, clr
  ROM #(.addrWidth(7), .dataWidth(1)) rom_1 (.addr(TestNumber), .data(Input));  // open: sel

  // Notes on the sheet:
  //   contents of rom_1 (hex, n*v repeats v):
  //   7*0 1 0 0 1 0 0 0 1 1 0 1 0 0 0 1 0 1 0 1 1 0 0 4*1 0 0 0 1 0 0 1 1 0 1 0 1 0 4*1 0 0 1 1 0 4*1 0
  //   4*1
endmodule

module Checker (
  input  Your_Answer,
  input  [6:0] TestNumber,
  output Correct,
  output Solution
);

  ROM #(.addrWidth(7), .dataWidth(1)) rom_1 (.addr(TestNumber), .data(Solution));  // open: sel
  Comparator #(.width(1)) comparator_1 (.a(Solution), .b(Your_Answer), .eq(Correct));  // open: gt, lt

  // Notes on the sheet:
  //   contents of rom_1 (hex, n*v repeats v):
  //   4*0 1 11*0 1 7*0 1 0 0 0 1 11*0 1 0 0 0 1 7*0 1 11*0 1
endmodule

module Sub_Circuit (
  input  A,
  input  B,
  input  C,
  input  D,
  input  \input ,
  output ns3,
  output ns2,
  output ns1,
  output ns0,
  output \output 
);

  wire and_1_out, and_2_out, and_3_out, and_4_out, and_5_out, and_6_out, and_7_out, and_8_out, and_9_out,
       and_10_out, and_11_out, and_12_out, and_13_out, and_14_out, not_1_out, not_2_out, not_3_out,
       not_4_out, not_5_out, not_6_out, not_7_out, not_8_out, not_9_out, not_10_out, not_11_out, not_12_out,
       not_13_out, not_14_out, not_15_out, not_16_out, not_17_out, not_18_out, not_19_out, not_20_out,
       not_21_out;

  not not_1 (not_1_out, C);
  not not_2 (not_2_out, D);
  not not_3 (not_3_out, \input );
  not not_4 (not_4_out, B);
  not not_5 (not_5_out, B);
  not not_6 (not_6_out, \input );
  not not_7 (not_7_out, C);
  not not_8 (not_8_out, \input );
  not not_9 (not_9_out, D);
  not not_10 (not_10_out, B);
  not not_11 (not_11_out, D);
  not not_12 (not_12_out, C);
  not not_13 (not_13_out, \input );
  not not_14 (not_14_out, C);
  not not_15 (not_15_out, \input );
  not not_16 (not_16_out, B);
  not not_17 (not_17_out, C);
  not not_18 (not_18_out, \input );
  not not_19 (not_19_out, \input );
  not not_20 (not_20_out, D);
  not not_21 (not_21_out, D);
  and and_1 (and_1_out, B, not_1_out, D, \input );
  and and_2 (and_2_out, B, C, not_2_out, not_3_out);
  and and_3 (and_3_out, not_4_out, D, \input );
  and and_4 (and_4_out, not_5_out, C, not_6_out);
  and and_5 (and_5_out, B, not_7_out, not_8_out);
  and and_6 (and_6_out, B, not_9_out, \input );
  and and_7 (and_7_out, not_10_out, not_11_out, \input );
  and and_8 (and_8_out, not_12_out, D, not_13_out);
  and and_9 (and_9_out, C, \input );
  and and_10 (and_10_out, B, not_14_out, not_15_out);
  and and_11 (and_11_out, not_16_out, not_17_out, not_18_out);
  and and_12 (and_12_out, D, not_19_out);
  and and_13 (and_13_out, C, not_20_out, \input );
  and and_14 (and_14_out, B, not_21_out, \input );
  or or_1 (ns3, and_1_out, and_2_out);
  or or_2 (ns2, and_3_out, and_4_out, and_5_out, and_6_out);
  or or_3 (ns1, and_7_out, and_8_out, and_9_out, and_10_out);
  or or_4 (ns0, and_11_out, and_12_out, and_13_out, and_14_out);
  and and_15 (\output , D, C, B);
endmodule
