// Logisim project Vending.circ as structural Verilog: 6 circuits, main circuit main
module main (
  input  Halt_Enable
);

  wire and_2_out, CLK, Correct, Dime, Done_Testing, Give_Dime, Give_Merch, Give_Nickel, Halt, Nickel,
       not_1_out, not_2_out, not_3_out, Quarter, Sol_Give_Dime, Sol_Give_Merch, Sol_Give_Nickel;
  wire [8:0] counter_1_q, TestNumber;

  Clock clock_1 (.out(CLK));
  not not_1 (not_1_out, Correct);
  and and_1 (Halt, Halt_Enable, not_1_out);
  Inputs inputs_1 (
    .Halt(Halt), .CLK(CLK), .Quarter(Quarter), .Dime(Dime), .Nickel(Nickel), .TestNumber(TestNumber),
    .Done_Testing(Done_Testing));
  // Probe on Quarter
  // Probe on Dime
  // Probe on Nickel
  Vending vending_1 (
    .Quarter(Quarter), .Dime(Dime), .Nickel(Nickel), .CLK(CLK), .Give_Dime(Give_Dime),
    .Give_Nickel(Give_Nickel), .Give_Merchandise(Give_Merch));
  // Probe on Correct
  // Probe on Give_Merch
  // Probe on Sol_Give_Merch
  // Probe on Give_Dime
  // Probe on Sol_Give_Dime
  // Probe on Give_Nickel
  // Probe on Sol_Give_Nickel
  not not_2 (not_2_out, Halt);
  Checker checker_1 (
    .Give_Merch(Give_Merch), .Give_Dime(Give_Dime), .Give_Nickel(Give_Nickel), .TestNumber(TestNumber),
    .Correct(Correct), .Sol_Give_Merch(Sol_Give_Merch), .Sol_Give_Dime(Sol_Give_Dime),
    .Sol_Give_Nickel(Sol_Give_Nickel));
  and and_2 (and_2_out, Correct, not_2_out, not_3_out);
  not not_3 (not_3_out, Done_Testing);
  Counter #(.width(9), .max('h162), .ongoal("stay")) counter_1 (
    .count(and_2_out), .Q(counter_1_q), .clk(CLK));  // open: load, D, carry, clr
  // Probe on counter_1_q

  // Notes on the sheet:
  //   Max 354
endmodule

module Vending (
  input  Quarter,
  input  Dime,
  input  Nickel,
  input  CLK,
  output Give_Merchandise,
  output Give_Dime,
  output Give_Nickel
);

  wire Out_A, Out_B, Out_C, X01, X10;

  Sub_Circuit__1 Sub_Circ__1 (.CLK(CLK), .PIN_1(X01), .PIN_2(X10), .Out_C(Out_C), .Out_B(Out_B), .Out_A(Out_A));
  Sub_Circuit__2 Sub_Circ__2 (
    .In_A(Out_A), .In_B(Out_B), .In_C(Out_C), .PIN_1(X01), .PIN_2(X10), .GM(Give_Merchandise),
    .GD(Give_Dime), .GN(Give_Nickel));
  and and_1 (X01, ~Quarter, ~Nickel);  // AND_Gate
  and and_2 (X10, ~Nickel, ~Dime);  // AND_Gate

  // Other names for the same wires on the sheet: Quater = Quarter
endmodule

module Inputs (
  input  Halt,
  input  CLK,
  output Quarter,
  output Dime,
  output Nickel,
  output [8:0] TestNumber,
  output Done_Testing
);

  wire not_1_out;

  not not_1 (not_1_out, Halt);
  Counter #(.width(9), .max('h162), .ongoal("stay")) counter_1 (
    .count(not_1_out), .Q(TestNumber), .carry(Done_Testing), .clk(CLK));  // open: load, D, clr
  ROM #(.addrWidth(9), .dataWidth(3)) rom_1 (.addr(TestNumber), .data({Quarter, Dime, Nickel}));  // open: sel

  // Notes on the sheet:
  //   contents of rom_1 (hex, n*v repeats v):
  //   1 0 1 0 1 0 1 0 1 0 1 0 1 0 1 0 1 0 1 0 1 0 2 0 1 0 1 0 1 0 1 0 1 0 4 0 1 0 1 0 1 0 1 0 2 0 1 0 1 0
  //   1 0 1 0 4 0 1 0 1 0 1 0 1 0 2 0 1 0 1 0 1 0 2 0 2 0 1 0 1 0 1 0 2 0 4 0 1 0 1 0 1 0 4 0 1 0 1 0 1 0
  //   1 0 2 0 1 0 1 0 1 0 2 0 2 0 1 0 1 0 1 0 2 0 4 0 1 0 1 0 2 0 2 0 1 0 1 0 2 0 4 0 1 0 1 0 4 0 1 0 1 0
  //   1 0 1 0 2 0 1 0 1 0 1 0 2 0 2 0 1 0 1 0 1 0 2 0 4 0 1 0 1 0 2 0 2 0 1 0 1 0 2 0 4 0 1 0 1 0 2 0 2 0
  //   1 0 2 0 2 0 2 0 1 0 2 0 2 0 4 0 1 0 2 0 4 0 1 0 4 0 1 0 1 0 1 0 1 0 2 0 1 0 1 0 1 0 2 0 2 0 1 0 1 0
  //   1 0 2 0 4 0 1 0 1 0 2 0 2 0 1 0 1 0 2 0 4 0 1 0 1 0 2 0 2 0 1 0 2 0 2 0 2 0 1 0 2 0 2 0 4 0 1 0 2 0
  //   4 0 1 0 1 0 2 0 2 0 1 0 2 0 2 0 2 0 1 0 2 0 2 0 4 0 2 0 2 0 2 0 2 0 2 0 4 0 2 0 4 0 1 0 4 0 2 0 4 0
  //   4 0 4
endmodule

module Checker (
  input  Give_Merch,
  input  Give_Dime,
  input  Give_Nickel,
  input  [8:0] TestNumber,
  output Correct,
  output Sol_Give_Merch,
  output Sol_Give_Dime,
  output Sol_Give_Nickel
);

  ROM #(.addrWidth(9), .dataWidth(3)) rom_1 (
    .addr(TestNumber), .data({Sol_Give_Merch, Sol_Give_Dime, Sol_Give_Nickel}));  // open: sel
  Comparator #(.width(3)) comparator_1 (
    .a({Sol_Give_Merch, Sol_Give_Dime, Sol_Give_Nickel}), .b({Give_Merch, Give_Dime, Give_Nickel}),
    .eq(Correct));  // open: gt, lt

  // Other names for the same wires on the sheet: Solution[2:0] = {Sol_Give_Merch, Sol_Give_Dime, Sol_Give_Nickel};
  //   Your_Answer[2:0] = {Give_Merch, Give_Dime, Give_Nickel}

  // Notes on the sheet:
  //   contents of rom_1 (hex, n*v repeats v):
  //   10*0 4 11*0 5 11*0 7 9*0 4 9*0 7 9*0 4 9*0 5 9*0 7 7*0 6 9*0 4 9*0 5 9*0 7 7*0 4 7*0 7 5*0 5 9*0 4
  //   9*0 5 9*0 7 7*0 4 7*0 7 7*0 4 7*0 5 7*0 7 5*0 6 0 0 0 4 9*0 4 9*0 5 9*0 7 7*0 4 7*0 7 7*0 4 7*0 5
  //   7*0 7 5*0 6 7*0 4 7*0 5 7*0 7 5*0 4 5*0 7 0 0 0 5 0 0 0 4 0 0 0 5 0 0 0 7
endmodule

module Sub_Circuit__1 (
  input  CLK,
  input  PIN_1,
  input  PIN_2,
  output Out_C,
  output Out_B,
  output Out_A
);

  wire and_1_out, and_2_out, and_3_out, and_4_out, and_5_out, and_6_out, and_7_out, and_8_out, and_9_out,
       and_10_out, and_11_out, and_12_out, not_1_out, not_2_out, not_3_out, not_4_out, not_5_out, not_6_out,
       not_7_out, not_8_out, not_9_out, not_10_out, not_11_out, not_12_out, not_13_out, not_14_out,
       not_15_out, not_16_out, not_17_out, not_18_out, not_19_out, or_1_out, or_2_out, or_3_out;

  not not_1 (not_1_out, PIN_1);
  not not_2 (not_2_out, PIN_1);
  not not_3 (not_3_out, PIN_2);
  not not_4 (not_4_out, Out_A);
  not not_5 (not_5_out, Out_B);
  not not_6 (not_6_out, PIN_1);
  not not_7 (not_7_out, PIN_2);
  not not_8 (not_8_out, Out_A);
  not not_9 (not_9_out, PIN_2);
  not not_10 (not_10_out, Out_A);
  not not_11 (not_11_out, PIN_2);
  not not_12 (not_12_out, PIN_1);
  not not_13 (not_13_out, Out_B);
  not not_14 (not_14_out, Out_C);
  not not_15 (not_15_out, PIN_1);
  not not_16 (not_16_out, PIN_2);
  not not_17 (not_17_out, PIN_2);
  not not_18 (not_18_out, PIN_2);
  not not_19 (not_19_out, PIN_1);
  and and_1 (and_1_out, Out_C, not_1_out);
  and and_2 (and_2_out, not_2_out, not_3_out);
  and and_3 (and_3_out, not_4_out, not_5_out, not_6_out);
  and and_4 (and_4_out, Out_A, Out_C, not_7_out);
  and and_5 (and_5_out, not_8_out, PIN_1, not_9_out);
  and and_6 (and_6_out, not_10_out, Out_C, not_11_out);
  and and_7 (and_7_out, Out_B, PIN_2, not_12_out);
  and and_8 (and_8_out, not_13_out, not_14_out, not_15_out, PIN_2);
  and and_9 (and_9_out, Out_B, not_16_out, PIN_1);
  and and_10 (and_10_out, Out_A, not_17_out, PIN_1);
  and and_11 (and_11_out, Out_B, not_18_out, Out_C);
  and and_12 (and_12_out, Out_A, Out_C, not_19_out);
  or or_1 (or_1_out, and_1_out, and_2_out, and_3_out, and_4_out);
  or or_2 (or_2_out, and_5_out, and_6_out, and_7_out);
  or or_3 (or_3_out, and_8_out, and_9_out, and_10_out, and_11_out, and_12_out);
  T_Flip_Flop t_ff_1 (.clk(CLK), .T(or_1_out), .Q(Out_C));  // open: Qn, preset, reset, en
  T_Flip_Flop t_ff_2 (.clk(CLK), .T(or_2_out), .Q(Out_B));  // open: Qn, preset, reset, en
  T_Flip_Flop t_ff_3 (.clk(CLK), .T(or_3_out), .Q(Out_A));  // open: Qn, preset, reset, en

  // Other names for the same wires on the sheet: In_Out_1 = Out_A; In_Out_2 = Out_B; In_Out_3 = Out_C
endmodule

module Sub_Circuit__2 (
  input  In_A,
  input  In_B,
  input  In_C,
  input  PIN_1,
  input  PIN_2,
  output GM,
  output GD,
  output GN
);

  wire and_1_out, and_2_out, and_3_out, and_4_out, and_5_out, and_6_out, and_7_out, and_8_out, and_9_out,
       and_10_out, not_1_out, not_2_out, not_3_out, not_4_out, not_5_out, not_6_out, not_7_out, not_8_out,
       not_9_out, not_10_out, not_11_out, not_12_out;

  not not_1 (not_1_out, PIN_1);
  not not_2 (not_2_out, In_B);
  not not_3 (not_3_out, PIN_1);
  not not_4 (not_4_out, In_C);
  not not_5 (not_5_out, PIN_1);
  not not_6 (not_6_out, PIN_1);
  not not_7 (not_7_out, PIN_2);
  and and_1 (and_1_out, In_B, PIN_2, not_8_out);
  not not_8 (not_8_out, PIN_1);
  and and_2 (and_2_out, In_C, PIN_2, not_9_out);
  not not_9 (not_9_out, PIN_1);
  and and_3 (and_3_out, In_A, not_10_out, PIN_1);
  not not_10 (not_10_out, PIN_2);
  and and_4 (and_4_out, In_A, PIN_2, not_11_out);
  not not_11 (not_11_out, PIN_1);
  and and_5 (and_5_out, In_A, In_C, not_12_out);
  not not_12 (not_12_out, PIN_2);
  and and_6 (and_6_out, In_B, In_C, not_1_out, PIN_2);
  and and_7 (and_7_out, In_A, not_2_out, not_3_out, PIN_2);
  and and_8 (and_8_out, In_B, not_4_out, PIN_2, not_5_out);
  and and_9 (and_9_out, In_A, PIN_2, not_6_out);
  and and_10 (and_10_out, In_A, In_C, not_7_out, PIN_1);
  or or_1 (GM, and_1_out, and_2_out, and_3_out, and_4_out, and_5_out);
  or or_2 (GD, and_6_out, and_7_out);
  or or_3 (GN, and_8_out, and_9_out, and_10_out);
endmodule
